# Fritzing sketch big-lantern (saved by Fritzing 0.9.3b)
perfboards: 1

parts:
  BAT1 = Battery Holders [package=battcom_20mm_pth]
  BAT2 = Battery Holders [package=battcom_20mm_pth]

nets:
  N1: BAT1.+, BAT2.+
  N2: BAT1.-, BAT2.-
